// Logisim project Evaluación 4 Fernando Mateo Valencia Gómez-Felipe Jose Benítez Avilez-Kenny Dong Jie Zhu Ye.circ as structural Verilog: 2 circuits, main circuit main
module main (
);

  wire _3, and_1_out, and_2_out, and_3_out, and_4_out, and_5_out, and_6_out, and_7_out, and_8_out, and_9_out,
       and_10_out, and_11_out, and_12_out, and_13_out, and_14_out, and_15_out, and_16_out, and_17_out,
       and_18_out, and_19_out, and_20_out, and_21_out, and_22_out, and_23_out, and_24_out, and_25_out,
       and_26_out, and_27_out, and_28_out, and_29_out, and_30_out, and_31_out, and_32_out, and_33_out,
       and_34_out, and_35_out, and_36_out, and_37_out, and_38_out, clock_1_out, controlled_buffer_1_out,
       d_ff_1_q, d_ff_1_qn, d_ff_2_q, d_ff_4_q, EMPEZAR_out, not_1_out, or_1_out, PERDIO;
  wire [4:0] counter_1_q, joystick_1_x, multiplexer_1_out, Pelota, random_1_out;
  wire [31:0] decoder_1_out31, demultiplexer_1_out0, demultiplexer_1_out1, demultiplexer_1_out2,
       demultiplexer_1_out3, demultiplexer_1_out4, demultiplexer_1_out5, demultiplexer_1_out6,
       demultiplexer_1_out7, demultiplexer_1_out8, demultiplexer_1_out9, demultiplexer_1_out10,
       demultiplexer_1_out11, demultiplexer_1_out12, demultiplexer_1_out13, demultiplexer_1_out14,
       demultiplexer_1_out15, demultiplexer_1_out16, demultiplexer_1_out17, demultiplexer_1_out18,
       demultiplexer_1_out19, demultiplexer_1_out20, demultiplexer_1_out21, demultiplexer_1_out22,
       demultiplexer_1_out23, demultiplexer_1_out24, demultiplexer_1_out25, demultiplexer_1_out26,
       demultiplexer_1_out27, demultiplexer_1_out28, demultiplexer_1_out29, demultiplexer_1_out30, Raqueta;

  Button EMPEZAR (.out(EMPEZAR_out));
  and and_1 (and_1_out, ~Pelota[0], ~Pelota[1], ~Pelota[2], ~Pelota[3], ~Pelota[4]);  // AND_Gate
  and and_2 (and_2_out, Pelota[0], Pelota[1], Pelota[2], Pelota[3], Pelota[4]);
  and and_3 (and_3_out, EMPEZAR_out, PERDIO);
  Random #(.width(5)) random_1 (.clk(and_3_out), .out(random_1_out));  // open: next, clr
  D_Flip_Flop d_ff_1 (.Q(d_ff_1_q), .Qn(d_ff_1_qn), .preset(and_2_out), .reset(and_1_out));  // open: clk, D, en
  Multiplexer #(.width(5)) multiplexer_1 (
    .in0(random_1_out), .in1(Pelota), .out(multiplexer_1_out), .sel(and_3_out));  // open: en
  and and_4 (and_4_out, ~counter_1_q[0], ~counter_1_q[1], ~counter_1_q[2], ~counter_1_q[3], ~counter_1_q[4]);  // AND_Gate
  and and_5 (and_5_out, counter_1_q[0], counter_1_q[1], counter_1_q[2], counter_1_q[3], counter_1_q[4]);
  Clock clock_1 (.out(clock_1_out));
  D_Flip_Flop d_ff_2 (.Q(d_ff_2_q), .preset(and_5_out), .reset(and_4_out));  // open: clk, D, Qn, en
  LED JUEGO (.in(PERDIO));
  D_Flip_Flop d_ff_3 (.Q(PERDIO), .preset(controlled_buffer_1_out), .reset(EMPEZAR_out));  // open: clk, D, Qn, en
  assign controlled_buffer_1_out = not_1_out ? _3 : 1'bz;  // Controlled_Buffer controlled_buffer_1
  not not_1 (not_1_out, EMPEZAR_out);
  Counter #(.width(5), .max('h1f)) counter_1 (
    .load(d_ff_2_q), .D(counter_1_q), .count(d_ff_4_q), .Q(counter_1_q), .clk(clock_1_out));  // open: carry, clr
  Joystick #(.bits(5)) joystick_1 (.x(joystick_1_x));  // open: y
  barra barra_1 (.in_1(joystick_1_x), .out_2(Raqueta));
  Counter #(.width(5), .max('h1f)) counter_2 (
    .load(d_ff_1_q), .D(multiplexer_1_out), .count(d_ff_4_q), .Q(Pelota), .clk(clock_1_out));  // open: carry, clr
  D_Flip_Flop d_ff_4 (
    .clk(clock_1_out), .Q(d_ff_4_q), .preset(EMPEZAR_out), .reset(controlled_buffer_1_out));  // open: D, Qn, en
  Decoder #(.select(5)) decoder_1 (
    .out0(decoder_1_out31[31]), .out1(decoder_1_out31[30]), .out2(decoder_1_out31[29]),
    .out3(decoder_1_out31[28]), .out4(decoder_1_out31[27]), .out5(decoder_1_out31[26]),
    .out6(decoder_1_out31[25]), .out7(decoder_1_out31[24]), .out8(decoder_1_out31[23]),
    .out9(decoder_1_out31[22]), .out10(decoder_1_out31[21]), .out11(decoder_1_out31[20]),
    .out12(decoder_1_out31[19]), .out13(decoder_1_out31[18]), .out14(decoder_1_out31[17]),
    .out15(decoder_1_out31[16]), .out16(decoder_1_out31[15]), .out17(decoder_1_out31[14]),
    .out18(decoder_1_out31[13]), .out19(decoder_1_out31[12]), .out20(decoder_1_out31[11]),
    .out21(decoder_1_out31[10]), .out22(decoder_1_out31[9]), .out23(decoder_1_out31[8]),
    .out24(decoder_1_out31[7]), .out25(decoder_1_out31[6]), .out26(decoder_1_out31[5]),
    .out27(decoder_1_out31[4]), .out28(decoder_1_out31[3]), .out29(decoder_1_out31[2]),
    .out30(decoder_1_out31[1]), .out31(decoder_1_out31[0]), .sel(counter_1_q));  // open: en
  Demultiplexer #(.select(5), .width(32)) demultiplexer_1 (
    .out0(demultiplexer_1_out0), .out1(demultiplexer_1_out1), .out2(demultiplexer_1_out2),
    .out3(demultiplexer_1_out3), .out4(demultiplexer_1_out4), .out5(demultiplexer_1_out5),
    .out6(demultiplexer_1_out6), .out7(demultiplexer_1_out7), .out8(demultiplexer_1_out8),
    .out9(demultiplexer_1_out9), .out10(demultiplexer_1_out10), .out11(demultiplexer_1_out11),
    .out12(demultiplexer_1_out12), .out13(demultiplexer_1_out13), .out14(demultiplexer_1_out14),
    .out15(demultiplexer_1_out15), .out16(demultiplexer_1_out16), .out17(demultiplexer_1_out17),
    .out18(demultiplexer_1_out18), .out19(demultiplexer_1_out19), .out20(demultiplexer_1_out20),
    .out21(demultiplexer_1_out21), .out22(demultiplexer_1_out22), .out23(demultiplexer_1_out23),
    .out24(demultiplexer_1_out24), .out25(demultiplexer_1_out25), .out26(demultiplexer_1_out26),
    .out27(demultiplexer_1_out27), .out28(demultiplexer_1_out28), .out29(demultiplexer_1_out29),
    .out30(demultiplexer_1_out30), .in(decoder_1_out31), .sel(Pelota));  // open: out31, en
  DotMatrix #(.inputtype("row"), .matrixcols(32), .matrixrows(32)) dotmatrix_1 (
    .row0(demultiplexer_1_out0), .row1(demultiplexer_1_out1), .row2(demultiplexer_1_out2),
    .row3(demultiplexer_1_out3), .row4(demultiplexer_1_out4), .row5(demultiplexer_1_out5),
    .row6(demultiplexer_1_out6), .row7(demultiplexer_1_out7), .row8(demultiplexer_1_out8),
    .row9(demultiplexer_1_out9), .row10(demultiplexer_1_out10), .row11(demultiplexer_1_out11),
    .row12(demultiplexer_1_out12), .row13(demultiplexer_1_out13), .row14(demultiplexer_1_out14),
    .row15(demultiplexer_1_out15), .row16(demultiplexer_1_out16), .row17(demultiplexer_1_out17),
    .row18(demultiplexer_1_out18), .row19(demultiplexer_1_out19), .row20(demultiplexer_1_out20),
    .row21(demultiplexer_1_out21), .row22(demultiplexer_1_out22), .row23(demultiplexer_1_out23),
    .row24(demultiplexer_1_out24), .row25(demultiplexer_1_out25), .row26(demultiplexer_1_out26),
    .row27(demultiplexer_1_out27), .row28(demultiplexer_1_out28), .row29(demultiplexer_1_out29),
    .row30(demultiplexer_1_out30), .row31(Raqueta));
  and and_6 (and_6_out, decoder_1_out31[0], Raqueta[0]);
  and and_7 (and_7_out, decoder_1_out31[1], Raqueta[1]);
  and and_8 (and_8_out, decoder_1_out31[2], Raqueta[2]);
  and and_9 (and_9_out, decoder_1_out31[3], Raqueta[3]);
  and and_10 (and_10_out, decoder_1_out31[4], Raqueta[4]);
  and and_11 (and_11_out, decoder_1_out31[5], Raqueta[5]);
  and and_12 (and_12_out, decoder_1_out31[6], Raqueta[6]);
  and and_13 (and_13_out, decoder_1_out31[7], Raqueta[7]);
  and and_14 (and_14_out, decoder_1_out31[8], Raqueta[8]);
  and and_15 (and_15_out, decoder_1_out31[9], Raqueta[9]);
  and and_16 (and_16_out, decoder_1_out31[10], Raqueta[10]);
  and and_17 (and_17_out, decoder_1_out31[11], Raqueta[11]);
  and and_18 (and_18_out, decoder_1_out31[12], Raqueta[12]);
  and and_19 (and_19_out, decoder_1_out31[13], Raqueta[13]);
  and and_20 (and_20_out, decoder_1_out31[14], Raqueta[14]);
  and and_21 (and_21_out, decoder_1_out31[15], Raqueta[15]);
  and and_22 (and_22_out, decoder_1_out31[16], Raqueta[16]);
  and and_23 (and_23_out, decoder_1_out31[17], Raqueta[17]);
  and and_24 (and_24_out, decoder_1_out31[18], Raqueta[18]);
  and and_25 (and_25_out, decoder_1_out31[19], Raqueta[19]);
  and and_26 (and_26_out, decoder_1_out31[20], Raqueta[20]);
  and and_27 (and_27_out, decoder_1_out31[21], Raqueta[21]);
  and and_28 (and_28_out, decoder_1_out31[22], Raqueta[22]);
  and and_29 (and_29_out, decoder_1_out31[23], Raqueta[23]);
  and and_30 (and_30_out, decoder_1_out31[24], Raqueta[24]);
  and and_31 (and_31_out, decoder_1_out31[25], Raqueta[25]);
  and and_32 (and_32_out, decoder_1_out31[26], Raqueta[26]);
  and and_33 (and_33_out, decoder_1_out31[27], Raqueta[27]);
  and and_34 (and_34_out, decoder_1_out31[28], Raqueta[28]);
  and and_35 (and_35_out, decoder_1_out31[29], Raqueta[29]);
  and and_36 (and_36_out, decoder_1_out31[30], Raqueta[30]);
  and and_37 (and_37_out, decoder_1_out31[31], Raqueta[31]);
  or or_1 (or_1_out, and_6_out, and_7_out, and_8_out, and_9_out, and_10_out, and_11_out, and_12_out, and_13_out, and_14_out, and_15_out, and_16_out, and_17_out, and_18_out, and_19_out, and_20_out, and_21_out, and_22_out, and_23_out, and_24_out, and_25_out, and_26_out, and_27_out, and_28_out, and_29_out, and_30_out, and_31_out, and_32_out, and_33_out, and_34_out, and_35_out, and_36_out, and_37_out);
  and and_38 (and_38_out, Pelota[0], Pelota[1], Pelota[2], Pelota[3], Pelota[4]);
  and and_39 (_3, and_38_out, ~or_1_out);  // AND_Gate

  // Notes on the sheet:
  //   No olvide activar el reloj
  //   Velocidad de reloj
  //   Facil 8Hz
  //   Normal 16Hz
  //   Dificil 32Hz
  //   Mientras este jugando la luz de JUEGO sera verde
  //   En caso de que la pelota caiga por abajo se detiene, y JUEGO sera roja
endmodule

module barra (
  input  [4:0] in_1,
  output [31:0] out_2
);

  wire decoder_1_out0, decoder_1_out1, decoder_1_out2, decoder_1_out3, decoder_1_out4, decoder_1_out5,
       decoder_1_out6, decoder_1_out7, decoder_1_out8, decoder_1_out9, decoder_1_out10, decoder_1_out11,
       decoder_1_out12, decoder_1_out13, decoder_1_out14, decoder_1_out15, decoder_1_out16, decoder_1_out17,
       decoder_1_out18, decoder_1_out19, decoder_1_out20, decoder_1_out21, decoder_1_out22, decoder_1_out23,
       decoder_1_out24, decoder_1_out25, decoder_1_out26, decoder_1_out27, decoder_1_out28, decoder_1_out29,
       decoder_1_out30, decoder_1_out31, decoder_2_out1, decoder_2_out2, decoder_2_out3, decoder_2_out4,
       decoder_2_out5, decoder_2_out6, decoder_2_out7, decoder_2_out8, decoder_2_out9, decoder_2_out10,
       decoder_2_out11, decoder_2_out12, decoder_2_out13, decoder_2_out14, decoder_2_out15, decoder_2_out16,
       decoder_2_out17, decoder_2_out18, decoder_2_out19, decoder_2_out20, decoder_2_out21, decoder_2_out22,
       decoder_2_out23, decoder_2_out24, decoder_2_out25, decoder_2_out26, decoder_2_out27, decoder_2_out28,
       decoder_2_out29, decoder_2_out30, decoder_2_out31, decoder_3_out2, decoder_3_out3, decoder_3_out4,
       decoder_3_out5, decoder_3_out6, decoder_3_out7, decoder_3_out8, decoder_3_out9, decoder_3_out10,
       decoder_3_out11, decoder_3_out12, decoder_3_out13, decoder_3_out14, decoder_3_out15, decoder_3_out16,
       decoder_3_out17, decoder_3_out18, decoder_3_out19, decoder_3_out20, decoder_3_out21, decoder_3_out22,
       decoder_3_out23, decoder_3_out24, decoder_3_out25, decoder_3_out26, decoder_3_out27, decoder_3_out28,
       decoder_3_out29, decoder_3_out30, decoder_3_out31, or_2_out, or_5_out;

  Decoder #(.select(5)) decoder_1 (
    .out0(decoder_1_out0), .out1(decoder_1_out1), .out2(decoder_1_out2), .out3(decoder_1_out3),
    .out4(decoder_1_out4), .out5(decoder_1_out5), .out6(decoder_1_out6), .out7(decoder_1_out7),
    .out8(decoder_1_out8), .out9(decoder_1_out9), .out10(decoder_1_out10), .out11(decoder_1_out11),
    .out12(decoder_1_out12), .out13(decoder_1_out13), .out14(decoder_1_out14), .out15(decoder_1_out15),
    .out16(decoder_1_out16), .out17(decoder_1_out17), .out18(decoder_1_out18), .out19(decoder_1_out19),
    .out20(decoder_1_out20), .out21(decoder_1_out21), .out22(decoder_1_out22), .out23(decoder_1_out23),
    .out24(decoder_1_out24), .out25(decoder_1_out25), .out26(decoder_1_out26), .out27(decoder_1_out27),
    .out28(decoder_1_out28), .out29(decoder_1_out29), .out30(decoder_1_out30), .out31(decoder_1_out31),
    .sel(in_1));  // open: en
  Decoder #(.select(5)) decoder_2 (
    .out1(decoder_2_out1), .out2(decoder_2_out2), .out3(decoder_2_out3), .out4(decoder_2_out4),
    .out5(decoder_2_out5), .out6(decoder_2_out6), .out7(decoder_2_out7), .out8(decoder_2_out8),
    .out9(decoder_2_out9), .out10(decoder_2_out10), .out11(decoder_2_out11), .out12(decoder_2_out12),
    .out13(decoder_2_out13), .out14(decoder_2_out14), .out15(decoder_2_out15), .out16(decoder_2_out16),
    .out17(decoder_2_out17), .out18(decoder_2_out18), .out19(decoder_2_out19), .out20(decoder_2_out20),
    .out21(decoder_2_out21), .out22(decoder_2_out22), .out23(decoder_2_out23), .out24(decoder_2_out24),
    .out25(decoder_2_out25), .out26(decoder_2_out26), .out27(decoder_2_out27), .out28(decoder_2_out28),
    .out29(decoder_2_out29), .out30(decoder_2_out30), .out31(decoder_2_out31), .sel(in_1));  // open: out0, en
  Decoder #(.select(5)) decoder_3 (
    .out2(decoder_3_out2), .out3(decoder_3_out3), .out4(decoder_3_out4), .out5(decoder_3_out5),
    .out6(decoder_3_out6), .out7(decoder_3_out7), .out8(decoder_3_out8), .out9(decoder_3_out9),
    .out10(decoder_3_out10), .out11(decoder_3_out11), .out12(decoder_3_out12), .out13(decoder_3_out13),
    .out14(decoder_3_out14), .out15(decoder_3_out15), .out16(decoder_3_out16), .out17(decoder_3_out17),
    .out18(decoder_3_out18), .out19(decoder_3_out19), .out20(decoder_3_out20), .out21(decoder_3_out21),
    .out22(decoder_3_out22), .out23(decoder_3_out23), .out24(decoder_3_out24), .out25(decoder_3_out25),
    .out26(decoder_3_out26), .out27(decoder_3_out27), .out28(decoder_3_out28), .out29(decoder_3_out29),
    .out30(decoder_3_out30), .out31(decoder_3_out31), .sel(in_1));  // open: out0, out1, en
  or or_1 (out_2[30], out_2[31], or_2_out);
  or or_2 (or_2_out, decoder_1_out1, decoder_2_out2, decoder_3_out3);
  or or_3 (out_2[31], decoder_1_out0, decoder_2_out1, decoder_3_out2);
  or or_4 (out_2[29], out_2[31], or_5_out);
  or or_5 (or_5_out, decoder_1_out2, decoder_2_out3, decoder_3_out4);
  or or_6 (out_2[27], decoder_1_out4, decoder_2_out5, decoder_3_out6);
  or or_7 (out_2[28], decoder_1_out3, decoder_2_out4, decoder_3_out5);
  or or_8 (out_2[26], decoder_1_out5, decoder_2_out6, decoder_3_out7);
  or or_9 (out_2[25], decoder_1_out6, decoder_2_out7, decoder_3_out8);
  or or_10 (out_2[22], decoder_1_out9, decoder_2_out10, decoder_3_out11);
  or or_11 (out_2[24], decoder_1_out7, decoder_2_out8, decoder_3_out9);
  or or_12 (out_2[23], decoder_1_out8, decoder_2_out9, decoder_3_out10);
  or or_13 (out_2[19], decoder_1_out12, decoder_2_out13, decoder_3_out14);
  or or_14 (out_2[20], decoder_1_out11, decoder_2_out12, decoder_3_out13);
  or or_15 (out_2[21], decoder_1_out10, decoder_2_out11, decoder_3_out12);
  or or_16 (out_2[18], decoder_1_out13, decoder_2_out14, decoder_3_out15);
  or or_17 (out_2[17], decoder_1_out14, decoder_2_out15, decoder_3_out16);
  or or_18 (out_2[15], decoder_1_out16, decoder_2_out17, decoder_3_out18);
  or or_19 (out_2[16], decoder_1_out15, decoder_2_out16, decoder_3_out17);
  or or_20 (out_2[14], decoder_1_out17, decoder_2_out18, decoder_3_out19);
  or or_21 (out_2[13], decoder_1_out18, decoder_2_out19, decoder_3_out20);
  or or_22 (out_2[12], decoder_1_out19, decoder_2_out20, decoder_3_out21);
  or or_23 (out_2[11], decoder_1_out20, decoder_2_out21, decoder_3_out22);
  or or_24 (out_2[9], decoder_1_out22, decoder_2_out23, decoder_3_out24);
  or or_25 (out_2[10], decoder_1_out21, decoder_2_out22, decoder_3_out23);
  or or_26 (out_2[6], decoder_1_out25, decoder_2_out26, decoder_3_out27);
  or or_27 (out_2[7], decoder_1_out24, decoder_2_out25, decoder_3_out26);
  or or_28 (out_2[8], decoder_1_out23, decoder_2_out24, decoder_3_out25);
  or or_29 (out_2[5], decoder_1_out26, decoder_2_out27, decoder_3_out28);
  or or_30 (out_2[3], decoder_1_out28, decoder_2_out29, decoder_3_out30);
  or or_31 (out_2[4], decoder_1_out27, decoder_2_out28, decoder_3_out29);
  or or_32 (out_2[2], decoder_1_out29, decoder_2_out30, decoder_3_out31);
  or or_33 (out_2[1], decoder_1_out30, decoder_2_out31);
  buf or_34 (out_2[0], decoder_1_out31);  // OR_Gate
endmodule
